# Fritzing sketch Circuit (saved by Fritzing 0.7.0b)
breadboards: 1

parts:
  Arduino_Ethernet_Shield1 = Arduino Ethernet Shield
  Button_1 = Pushbutton [package=THT]
  Button_2 = Pushbutton [package=THT]
  Button_3 = Pushbutton [package=THT]
  Button_4 = Pushbutton [package=THT]
  Stop_Button = Pushbutton [package=THT]
  Red_LED = LED - 5mm [color="Red (633nm)" package="5 mm [THT]"]
  Red_LED_Resistor = Resistor [tolerance=±5% resistance=560 package=THT]
  Green_LED = LED - 5mm [color="Green (555nm)" package="5 mm [THT]"]
  Green_LED_Resistor = Resistor [tolerance=±5% resistance=560 package=THT]

nets:
  N1: Arduino_Ethernet_Shield1.D9, Red_LED.anode
  N2: Arduino_Ethernet_Shield1.D8, Green_LED.anode
  N3: Arduino_Ethernet_Shield1.D7, Stop_Button.leg0
  N4: Arduino_Ethernet_Shield1.D6, Button_4.leg0
  N5: Arduino_Ethernet_Shield1.D5, Button_3.leg0
  N6: Arduino_Ethernet_Shield1.D3, Button_2.leg0
  N7: Arduino_Ethernet_Shield1.D2, Button_1.leg0
  N8: Arduino_Ethernet_Shield1.GND, Button_1.leg1, Button_2.leg1, Button_3.leg1, Button_4.leg1, Stop_Button.leg1, Red_LED_Resistor.Pin_1, Green_LED_Resistor.Pin_1
  N9: Red_LED.cathode, Red_LED_Resistor.Pin_0
  N10: Green_LED.cathode, Green_LED_Resistor.Pin_0
